# Fritzing sketch IoTRack (saved by Fritzing 0.9.3b)

parts:
  Bauteil4 = Adafruit Feather 328P [part_number="Adafruit #3458"]
  PART1 = APDS-9960 RGB and Gesture Sensor [part_number=SEN-12787]
  PART2 = APDS-9960 RGB and Gesture Sensor [part_number=SEN-12787]
  PART3 = APDS-9960 RGB and Gesture Sensor [part_number=SEN-12787]

nets:
  N1: Bauteil4.A3, PART1.SDA
  N2: Bauteil4.A2, PART2.SDA
  N3: Bauteil4.A1, PART3.SDA
  N4: Bauteil4.A0, PART1.SCL, PART2.SCL, PART3.SCL
  GND: Bauteil4.GND, PART1.GND, PART2.GND, PART3.GND
  VCC: Bauteil4.3.3V, PART1.VCC, PART2.VCC, PART3.VCC
  N5: Bauteil4.D5, PART1.INT, PART2.INT, PART3.INT

custom parts:
  Adafruit Feather 328P: With this Feather we're getting a little nostalgic for the ATmega328P - the classic 'Arduino' chip - with this Adafruit Feather 328P running a 3.3V and 8 MHz. Feather is the new development board from Adafruit, and like it's namesake it is thin, light, and lets you fly! We designed Feather to be a new standard for portable microcontroller cores. We have other boards in the Feather family,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
  APDS-9960 RGB and Gesture Sensor: Breakout board for the Avago APDS-9960 proximity, light, RGB, and gesture sensors. Please visit www.sparkfun.com to learn more.
